// Logisim project 8-Bit Caculator, Assignment 1.circ as structural Verilog: 9 circuits, main circuit Stage_4
module Stage_1 (
  input  in_1,
  input  in_2,
  input  in_3,
  input  Input_A,
  input  in_5,
  input  in_6,
  input  in_7,
  input  in_8,
  input  in_9,
  input  in_10,
  input  in_11,
  input  Input_B,
  input  in_13,
  input  in_14,
  input  in_15,
  input  in_16
);

  wire button_1_out, button_2_out;
  wire [7:0] load_and_reset_1_out_4, load_and_reset_2_out_4;

  Button button_1 (.out(button_1_out));
  Button button_2 (.out(button_2_out));
  Load_And_Reset load_and_reset_1 (
    .Load(button_1_out), .Reset(button_2_out), .Aor_B({in_8, in_7, in_6, in_5, Input_A, in_3, in_2, in_1}),
    .out_4(load_and_reset_1_out_4));
  LED led_1 (.in(load_and_reset_1_out_4[7]));
  Load_And_Reset load_and_reset_2 (
    .Load(button_1_out), .Reset(button_2_out),
    .Aor_B({in_16, in_15, in_14, in_13, Input_B, in_11, in_10, in_9}), .out_4(load_and_reset_2_out_4));
  LED led_2 (.in(load_and_reset_2_out_4[7]));
  LED led_3 (.in(load_and_reset_1_out_4[6]));
  LED led_4 (.in(load_and_reset_1_out_4[5]));
  LED led_5 (.in(load_and_reset_1_out_4[4]));
  LED led_6 (.in(load_and_reset_2_out_4[6]));
  LED led_7 (.in(load_and_reset_2_out_4[5]));
  LED led_8 (.in(load_and_reset_2_out_4[4]));
  LED led_9 (.in(load_and_reset_1_out_4[3]));
  LED led_10 (.in(load_and_reset_1_out_4[2]));
  LED led_11 (.in(load_and_reset_2_out_4[3]));
  LED led_12 (.in(load_and_reset_2_out_4[2]));
  LED led_13 (.in(load_and_reset_1_out_4[1]));
  LED led_14 (.in(load_and_reset_1_out_4[0]));
  LED led_15 (.in(load_and_reset_2_out_4[1]));
  LED led_16 (.in(load_and_reset_2_out_4[0]));

  // Notes on the sheet:
  //   Load
  //   Reset
  //   Stage 1: Load and Reset
  //   Input A Display
  //   Input B Display
endmodule

module Load_And_Reset (
  input  Load,
  input  Reset,
  input  [7:0] Aor_B,
  output [7:0] out_4
);

  D_Flip_Flop d_ff_1 (.D(Aor_B[0]), .clk(Load), .Q(out_4[0]), .reset(Reset));  // open: Qn, preset
  D_Flip_Flop d_ff_2 (.D(Aor_B[1]), .clk(Load), .Q(out_4[1]), .reset(Reset));  // open: Qn, preset
  D_Flip_Flop d_ff_3 (.D(Aor_B[2]), .clk(Load), .Q(out_4[2]), .reset(Reset));  // open: Qn, preset
  D_Flip_Flop d_ff_4 (.D(Aor_B[3]), .clk(Load), .Q(out_4[3]), .reset(Reset));  // open: Qn, preset
  D_Flip_Flop d_ff_5 (.D(Aor_B[4]), .clk(Load), .Q(out_4[4]), .reset(Reset));  // open: Qn, preset
  D_Flip_Flop d_ff_6 (.D(Aor_B[5]), .clk(Load), .Q(out_4[5]), .reset(Reset));  // open: Qn, preset
  D_Flip_Flop d_ff_7 (.D(Aor_B[6]), .clk(Load), .Q(out_4[6]), .reset(Reset));  // open: Qn, preset
  D_Flip_Flop d_ff_8 (.D(Aor_B[7]), .clk(Load), .Q(out_4[7]), .reset(Reset));  // open: Qn, preset
endmodule

module Stage_2 (
  input  in_1,
  input  in_2,
  input  in_3,
  input  Input_A,
  input  in_5,
  input  in_6,
  input  in_7,
  input  in_8,
  input  in_9,
  input  in_10,
  input  in_11,
  input  Input_B,
  input  in_13,
  input  in_14,
  input  in_15,
  input  in_16
);

  wire button_1_out, button_2_out, button_3_out, undriven;
  wire [7:0] eight_bit_adder_1_out_6, load_and_reset_1_out_4, load_and_reset_2_out_4;

  Button button_1 (.out(button_1_out));
  Button button_2 (.out(button_2_out));
  Button button_3 (.out(button_3_out));
  Load_And_Reset load_and_reset_1 (
    .Load(button_1_out), .Reset(button_2_out), .Aor_B({in_8, in_7, in_6, in_5, Input_A, in_3, in_2, in_1}),
    .out_4(load_and_reset_1_out_4));
  LED led_1 (.in(load_and_reset_1_out_4[7]));
  Eight_Bit_Adder eight_bit_adder_1 (
    .Plus(button_3_out), .A(load_and_reset_1_out_4), .Reset(button_2_out), .B(load_and_reset_2_out_4),
    .Pos_OR_Neg(undriven), .out_6(eight_bit_adder_1_out_6));
  LED led_2 (.in(eight_bit_adder_1_out_6[7]));
  LED led_3 (.in(undriven));
  Load_And_Reset load_and_reset_2 (
    .Load(button_1_out), .Reset(button_2_out),
    .Aor_B({in_16, in_15, in_14, in_13, Input_B, in_11, in_10, in_9}), .out_4(load_and_reset_2_out_4));
  LED led_4 (.in(load_and_reset_2_out_4[7]));
  LED led_5 (.in(load_and_reset_1_out_4[6]));
  LED led_6 (.in(load_and_reset_1_out_4[5]));
  LED led_7 (.in(load_and_reset_1_out_4[4]));
  LED led_8 (.in(eight_bit_adder_1_out_6[6]));
  LED led_9 (.in(eight_bit_adder_1_out_6[5]));
  LED led_10 (.in(eight_bit_adder_1_out_6[4]));
  LED led_11 (.in(load_and_reset_2_out_4[6]));
  LED led_12 (.in(load_and_reset_2_out_4[5]));
  LED led_13 (.in(load_and_reset_2_out_4[4]));
  LED led_14 (.in(load_and_reset_1_out_4[3]));
  LED led_15 (.in(load_and_reset_1_out_4[2]));
  LED led_16 (.in(eight_bit_adder_1_out_6[3]));
  LED led_17 (.in(eight_bit_adder_1_out_6[2]));
  LED led_18 (.in(load_and_reset_2_out_4[3]));
  LED led_19 (.in(load_and_reset_2_out_4[2]));
  LED led_20 (.in(load_and_reset_1_out_4[1]));
  LED led_21 (.in(load_and_reset_1_out_4[0]));
  LED led_22 (.in(eight_bit_adder_1_out_6[1]));
  LED led_23 (.in(eight_bit_adder_1_out_6[0]));
  LED led_24 (.in(load_and_reset_2_out_4[1]));
  LED led_25 (.in(load_and_reset_2_out_4[0]));

  // Notes on the sheet:
  //   Load
  //   Reset
  //   Add
  //   8-bit Adder
  //   +/-
  //   Input A Display
  //   Input B Display
endmodule

module Full_Adder (
  input  C_In,
  input  A,
  input  B,
  output Sum,
  output C_Out
);

  wire and_1_out, and_2_out, xor_1_out;

  xor xor_1 (xor_1_out, A, B);
  and and_1 (and_1_out, B, A);
  xor xor_2 (Sum, C_In, xor_1_out);
  and and_2 (and_2_out, C_In, xor_1_out);
  or or_1 (C_Out, and_2_out, and_1_out);
endmodule

module Eight_Bit_Adder (
  input  Plus,
  input  [7:0] A,
  input  Reset,
  input  [7:0] B,
  input  Pos_OR_Neg,
  output [7:0] out_6
);

  wire and_1_out, full_adder_1_c_out, full_adder_2_c_out, full_adder_3_c_out, full_adder_4_c_out,
       full_adder_5_c_out, full_adder_6_c_out;
  wire [7:0] load_and_reset_1_out_4, load_and_reset_2_out_4;

  Load_And_Reset load_and_reset_1 (.Load(Plus), .Reset(Reset), .Aor_B(A), .out_4(load_and_reset_1_out_4));
  Load_And_Reset load_and_reset_2 (.Load(Plus), .Reset(Reset), .Aor_B(B), .out_4(load_and_reset_2_out_4));
  xor xor_1 (out_6[0], load_and_reset_1_out_4[0], load_and_reset_2_out_4[0]);
  and and_1 (and_1_out, load_and_reset_2_out_4[0], load_and_reset_1_out_4[0]);
  Full_Adder full_adder_1 (
    .C_In(and_1_out), .A(load_and_reset_1_out_4[1]), .B(load_and_reset_2_out_4[1]), .Sum(out_6[1]),
    .C_Out(full_adder_1_c_out));
  Full_Adder full_adder_2 (
    .C_In(full_adder_1_c_out), .A(load_and_reset_1_out_4[2]), .B(load_and_reset_2_out_4[2]), .Sum(out_6[2]),
    .C_Out(full_adder_2_c_out));
  Full_Adder full_adder_3 (
    .C_In(full_adder_2_c_out), .A(load_and_reset_1_out_4[3]), .B(load_and_reset_2_out_4[3]), .Sum(out_6[3]),
    .C_Out(full_adder_3_c_out));
  Full_Adder full_adder_4 (
    .C_In(full_adder_3_c_out), .A(load_and_reset_1_out_4[4]), .B(load_and_reset_2_out_4[4]), .Sum(out_6[4]),
    .C_Out(full_adder_4_c_out));
  Full_Adder full_adder_5 (
    .C_In(full_adder_4_c_out), .A(load_and_reset_1_out_4[5]), .B(load_and_reset_2_out_4[5]), .Sum(out_6[5]),
    .C_Out(full_adder_5_c_out));
  Full_Adder full_adder_6 (
    .C_In(full_adder_5_c_out), .A(load_and_reset_1_out_4[6]), .B(load_and_reset_2_out_4[6]), .Sum(out_6[6]),
    .C_Out(full_adder_6_c_out));
  Full_Adder full_adder_7 (
    .C_In(full_adder_6_c_out), .A(load_and_reset_1_out_4[7]), .B(load_and_reset_2_out_4[7]), .Sum(Pos_OR_Neg));  // open: C_Out

  assign out_6[7] = Pos_OR_Neg;
endmodule

module Stage_3 (
  input  in_1,
  input  in_2,
  input  in_3,
  input  Input_A,
  input  in_5,
  input  in_6,
  input  in_7,
  input  in_8,
  input  in_9,
  input  in_10,
  input  in_11,
  input  Input_B,
  input  in_13,
  input  in_14,
  input  in_15,
  input  in_16
);

  wire button_1_out, button_2_out, button_3_out, button_4_out, button_5_out, undriven, undriven_2, undriven_3;
  wire [7:0] eight_bit_adder_1_out_6, load_and_reset_1_out_4, load_and_reset_2_out_4, make_negative_1_out_5,
       make_negative_2_out_5;

  Button button_1 (.out(button_1_out));
  Button button_2 (.out(button_2_out));
  Button button_3 (.out(button_3_out));
  Button button_4 (.out(button_4_out));
  LED led_1 (.in(undriven));
  LED led_2 (.in(undriven_2));
  Load_And_Reset load_and_reset_1 (
    .Load(button_1_out), .Reset(button_2_out), .Aor_B({in_8, in_7, in_6, in_5, Input_A, in_3, in_2, in_1}),
    .out_4(load_and_reset_1_out_4));
  Make_Negative make_negative_1 (
    .Post_Neg_Button(button_4_out), .Reset(button_2_out), .The_Input(load_and_reset_1_out_4),
    .Pos_OR_Neg(undriven), .out_5(make_negative_1_out_5));
  Load_And_Reset load_and_reset_2 (
    .Load(button_1_out), .Reset(button_2_out),
    .Aor_B({in_16, in_15, in_14, in_13, Input_B, in_11, in_10, in_9}), .out_4(load_and_reset_2_out_4));
  Make_Negative make_negative_2 (
    .Post_Neg_Button(button_5_out), .Reset(button_2_out), .The_Input(load_and_reset_2_out_4),
    .Pos_OR_Neg(undriven_2), .out_5(make_negative_2_out_5));
  LED led_3 (.in(make_negative_1_out_5[7]));
  LED led_4 (.in(make_negative_1_out_5[6]));
  LED led_5 (.in(make_negative_1_out_5[5]));
  LED led_6 (.in(make_negative_2_out_5[7]));
  LED led_7 (.in(make_negative_2_out_5[6]));
  LED led_8 (.in(make_negative_2_out_5[5]));
  LED led_9 (.in(make_negative_1_out_5[4]));
  LED led_10 (.in(make_negative_1_out_5[3]));
  LED led_11 (.in(make_negative_1_out_5[2]));
  LED led_12 (.in(make_negative_2_out_5[4]));
  LED led_13 (.in(make_negative_2_out_5[3]));
  LED led_14 (.in(make_negative_1_out_5[1]));
  LED led_15 (.in(make_negative_1_out_5[0]));
  LED led_16 (.in(make_negative_2_out_5[2]));
  LED led_17 (.in(make_negative_2_out_5[1]));
  LED led_18 (.in(make_negative_2_out_5[0]));
  LED led_19 (.in(undriven_3));
  Button button_5 (.out(button_5_out));
  Eight_Bit_Adder eight_bit_adder_1 (
    .Plus(button_3_out), .A(make_negative_1_out_5), .Reset(button_2_out), .B(make_negative_2_out_5),
    .Pos_OR_Neg(undriven_3), .out_6(eight_bit_adder_1_out_6));
  LED led_20 (.in(eight_bit_adder_1_out_6[7]));
  LED led_21 (.in(eight_bit_adder_1_out_6[6]));
  LED led_22 (.in(eight_bit_adder_1_out_6[5]));
  LED led_23 (.in(eight_bit_adder_1_out_6[4]));
  LED led_24 (.in(eight_bit_adder_1_out_6[3]));
  LED led_25 (.in(eight_bit_adder_1_out_6[2]));
  LED led_26 (.in(eight_bit_adder_1_out_6[1]));
  LED led_27 (.in(eight_bit_adder_1_out_6[0]));

  // Notes on the sheet:
  //   Load
  //   Reset
  //   Add
  //   +/-
  //   +/-
  //   +/-
  //   2's Compliments
  //   Input B Display
  //   +/-
  //   +/-
  //   Input A Display
endmodule

module Make_Negative (
  input  Post_Neg_Button,
  input  Reset,
  input  [7:0] The_Input,
  input  Pos_OR_Neg,
  output [7:0] out_5
);

  wire and_1_out, and_2_out, and_3_out, and_4_out, and_5_out, and_6_out, and_7_out, and_8_out, and_9_out,
       and_10_out, and_11_out, and_12_out, and_13_out, and_14_out, and_15_out, and_16_out, not_1_out,
       not_2_out, not_3_out, not_4_out, not_5_out, not_6_out, not_7_out, not_8_out, not_9_out, not_10_out,
       not_11_out, not_12_out, not_13_out, not_14_out, not_15_out, not_16_out;
  wire [7:0] or_1_out, t_ff_1_q;

  T_Flip_Flop t_ff_1 (.T(1'b1), .clk(Post_Neg_Button), .Q(t_ff_1_q[0]), .reset(Reset));  // open: Qn, preset
  not not_1 (not_1_out, t_ff_1_q[0]);
  not not_2 (not_2_out, t_ff_1_q[0]);
  not not_3 (not_3_out, The_Input[3]);
  not not_4 (not_4_out, t_ff_1_q[0]);
  not not_5 (not_5_out, The_Input[4]);
  not not_6 (not_6_out, t_ff_1_q[0]);
  not not_7 (not_7_out, The_Input[5]);
  not not_8 (not_8_out, t_ff_1_q[0]);
  not not_9 (not_9_out, The_Input[6]);
  not not_10 (not_10_out, t_ff_1_q[0]);
  not not_11 (not_11_out, The_Input[7]);
  and and_1 (and_1_out, The_Input[0], not_12_out);
  not not_12 (not_12_out, t_ff_1_q[0]);
  not not_13 (not_13_out, The_Input[0]);
  and and_2 (and_2_out, not_13_out, t_ff_1_q[0]);
  and and_3 (and_3_out, The_Input[1], not_14_out);
  not not_14 (not_14_out, t_ff_1_q[0]);
  not not_15 (not_15_out, The_Input[1]);
  and and_4 (and_4_out, not_15_out, t_ff_1_q[0]);
  and and_5 (and_5_out, The_Input[2], not_1_out);
  not not_16 (not_16_out, The_Input[2]);
  and and_6 (and_6_out, not_16_out, t_ff_1_q[0]);
  and and_7 (and_7_out, The_Input[3], not_2_out);
  and and_8 (and_8_out, not_3_out, t_ff_1_q[0]);
  and and_9 (and_9_out, The_Input[4], not_4_out);
  and and_10 (and_10_out, not_5_out, t_ff_1_q[0]);
  and and_11 (and_11_out, The_Input[5], not_6_out);
  and and_12 (and_12_out, not_7_out, t_ff_1_q[0]);
  and and_13 (and_13_out, The_Input[6], not_8_out);
  and and_14 (and_14_out, not_9_out, t_ff_1_q[0]);
  and and_15 (and_15_out, The_Input[7], not_10_out);
  and and_16 (and_16_out, not_11_out, t_ff_1_q[0]);
  or or_1 (or_1_out[0], and_1_out, and_2_out);
  or or_2 (or_1_out[1], and_3_out, and_4_out);
  or or_3 (or_1_out[2], and_5_out, and_6_out);
  or or_4 (or_1_out[3], and_7_out, and_8_out);
  or or_5 (or_1_out[4], and_9_out, and_10_out);
  or or_6 (or_1_out[5], and_11_out, and_12_out);
  or or_7 (or_1_out[6], and_13_out, and_14_out);
  or or_8 (or_1_out[7], and_15_out, and_16_out);
  Eight_Bit_Adder_Without_Register eight_bit_adder_without_register_1 (
    .A(or_1_out), .B(t_ff_1_q), .Pos_OR_Neg(Pos_OR_Neg), .out_4(out_5));
endmodule

module Stage_4 (
  input  in_1,
  input  in_2,
  input  in_3,
  input  Input_A,
  input  in_5,
  input  in_6,
  input  in_7,
  input  in_8,
  input  in_9,
  input  in_10,
  input  in_11,
  input  Input_B,
  input  in_13,
  input  in_14,
  input  in_15,
  input  in_16
);

  wire button_1_out, button_2_out, button_3_out, button_4_out, button_5_out, button_6_out, d_ff_1_q,
       d_ff_2_q, or_1_out, or_2_out, undriven, undriven_2, undriven_3;
  wire [7:0] eight_bit_adder_1_out_6, load_and_reset_1_out_4, load_and_reset_2_out_4, make_negative_1_out_5,
       make_negative_2_out_5;

  Button button_1 (.out(button_1_out));
  Button button_2 (.out(button_2_out));
  Button button_3 (.out(button_3_out));
  Button button_4 (.out(button_4_out));
  LED led_1 (.in(undriven));
  LED led_2 (.in(undriven_2));
  Load_And_Reset load_and_reset_1 (
    .Load(button_1_out), .Reset(button_2_out), .Aor_B({in_8, in_7, in_6, in_5, Input_A, in_3, in_2, in_1}),
    .out_4(load_and_reset_1_out_4));
  Make_Negative make_negative_1 (
    .Post_Neg_Button(button_4_out), .Reset(button_2_out), .The_Input(load_and_reset_1_out_4),
    .Pos_OR_Neg(undriven), .out_5(make_negative_1_out_5));
  LED led_3 (.in(make_negative_1_out_5[7]));
  Load_And_Reset load_and_reset_2 (
    .Load(button_1_out), .Reset(button_2_out),
    .Aor_B({in_16, in_15, in_14, in_13, Input_B, in_11, in_10, in_9}), .out_4(load_and_reset_2_out_4));
  Make_Negative make_negative_2 (
    .Post_Neg_Button(or_2_out), .Reset(button_2_out), .The_Input(load_and_reset_2_out_4),
    .Pos_OR_Neg(undriven_2), .out_5(make_negative_2_out_5));
  LED led_4 (.in(make_negative_1_out_5[6]));
  LED led_5 (.in(make_negative_1_out_5[5]));
  LED led_6 (.in(make_negative_2_out_5[7]));
  LED led_7 (.in(make_negative_2_out_5[6]));
  LED led_8 (.in(make_negative_2_out_5[5]));
  LED led_9 (.in(make_negative_1_out_5[4]));
  LED led_10 (.in(make_negative_1_out_5[3]));
  LED led_11 (.in(make_negative_1_out_5[2]));
  or or_1 (or_1_out, d_ff_2_q, button_3_out);
  Button button_5 (.out(button_5_out));
  LED led_12 (.in(make_negative_2_out_5[4]));
  LED led_13 (.in(make_negative_2_out_5[3]));
  LED led_14 (.in(make_negative_2_out_5[2]));
  LED led_15 (.in(make_negative_1_out_5[1]));
  LED led_16 (.in(make_negative_1_out_5[0]));
  LED led_17 (.in(make_negative_2_out_5[1]));
  LED led_18 (.in(make_negative_2_out_5[0]));
  LED led_19 (.in(undriven_3));
  D_Flip_Flop d_ff_1 (.D(1'b1), .clk(button_5_out), .Q(d_ff_1_q), .reset(button_2_out));  // open: Qn, preset
  D_Flip_Flop #(.trigger("falling")) d_ff_2 (
    .D(1'b1), .clk(button_5_out), .Q(d_ff_2_q), .reset(button_2_out));  // open: Qn, preset
  Button button_6 (.out(button_6_out));
  Eight_Bit_Adder eight_bit_adder_1 (
    .Plus(or_1_out), .A(make_negative_1_out_5), .Reset(button_2_out), .B(make_negative_2_out_5),
    .Pos_OR_Neg(undriven_3), .out_6(eight_bit_adder_1_out_6));
  or or_2 (or_2_out, button_6_out, d_ff_1_q);
  LED led_20 (.in(eight_bit_adder_1_out_6[7]));
  LED led_21 (.in(eight_bit_adder_1_out_6[6]));
  LED led_22 (.in(eight_bit_adder_1_out_6[5]));
  LED led_23 (.in(eight_bit_adder_1_out_6[4]));
  LED led_24 (.in(eight_bit_adder_1_out_6[3]));
  LED led_25 (.in(eight_bit_adder_1_out_6[2]));
  LED led_26 (.in(eight_bit_adder_1_out_6[1]));
  LED led_27 (.in(eight_bit_adder_1_out_6[0]));

  // Notes on the sheet:
  //   Load
  //   Reset
  //   Add
  //   +/-
  //   +/-
  //   +/-
  //   Subtract
  //   Input B Display
  //   +/-
  //   +/-
  //   Input A Display
endmodule

module Eight_Bit_Adder_Without_Register (
  input  [7:0] A,
  input  [7:0] B,
  input  Pos_OR_Neg,
  output [7:0] out_4
);

  wire and_1_out, full_adder_1_c_out, full_adder_2_c_out, full_adder_3_c_out, full_adder_4_c_out,
       full_adder_5_c_out, full_adder_6_c_out;

  xor xor_1 (out_4[0], A[0], B[0]);
  and and_1 (and_1_out, B[0], A[0]);
  Full_Adder full_adder_1 (.C_In(and_1_out), .A(A[1]), .B(B[1]), .Sum(out_4[1]), .C_Out(full_adder_1_c_out));
  Full_Adder full_adder_2 (.C_In(full_adder_1_c_out), .A(A[2]), .B(B[2]), .Sum(out_4[2]), .C_Out(full_adder_2_c_out));
  Full_Adder full_adder_3 (.C_In(full_adder_2_c_out), .A(A[3]), .B(B[3]), .Sum(out_4[3]), .C_Out(full_adder_3_c_out));
  Full_Adder full_adder_4 (.C_In(full_adder_3_c_out), .A(A[4]), .B(B[4]), .Sum(out_4[4]), .C_Out(full_adder_4_c_out));
  Full_Adder full_adder_5 (.C_In(full_adder_4_c_out), .A(A[5]), .B(B[5]), .Sum(out_4[5]), .C_Out(full_adder_5_c_out));
  Full_Adder full_adder_6 (.C_In(full_adder_5_c_out), .A(A[6]), .B(B[6]), .Sum(out_4[6]), .C_Out(full_adder_6_c_out));
  Full_Adder full_adder_7 (.C_In(full_adder_6_c_out), .A(A[7]), .B(B[7]), .Sum(Pos_OR_Neg));  // open: C_Out

  assign out_4[7] = Pos_OR_Neg;
endmodule
