// Logisim project stage1.circ as structural Verilog: 2 circuits, main circuit main
module main (
);

  wire button_1_out, ioclock_1_clockstatus;

  Button button_1 (.out(button_1_out));
  Hex_Digit_Display hex_digit_display_1 ();  // open: value, dp
  Button button_2 ();  // open: out
  Hex_Digit_Display hex_digit_display_2 ();  // open: value, dp
  Button button_3 ();  // open: out
  Hex_Digit_Display hex_digit_display_3 ();  // open: value, dp
  Hex_Digit_Display hex_digit_display_4 ();  // open: value, dp
  ioClock ioclock_1 (.CTRLButton(button_1_out), .CLOCKStatus(ioclock_1_clockstatus));
  Hex_Digit_Display hex_digit_display_5 ();  // open: value, dp
  Hex_Digit_Display hex_digit_display_6 ();  // open: value, dp
  LED led_1 (.in(ioclock_1_clockstatus));
  Hex_Digit_Display hex_digit_display_7 ();  // open: value, dp
  Hex_Digit_Display hex_digit_display_8 ();  // open: value, dp

  // Notes on the sheet:
  //   Start / Stop
  //   Split
  //   Elapsed Time
  //   Minutes
  //   :
  //   Reset
  //   Seconds
  //   Stopwatch Interface
  //   Minutes
  //   Clock Started
  //   Split Time
  //   :
  //   Seconds
endmodule

module ioClock (
  input  CTRLButton,
  output CLOCKStatus
);

  T_Flip_Flop t_ff_1 (.T(CTRLButton), .clk(CTRLButton), .Q(CLOCKStatus));  // open: Qn, reset, preset
endmodule
