// Logisim project stage2.circ as structural Verilog: 6 circuits, main circuit main
module main (
);

  wire button_1_out, clockcircuit_1_clockstatus;
  wire [3:0] clockcircuit_1_firstdigit, clockcircuit_1_seconddigit;

  Button button_1 (.out(button_1_out));
  Hex_Digit_Display hex_digit_display_1 ();  // open: value, dp
  Button button_2 ();  // open: out
  Hex_Digit_Display hex_digit_display_2 ();  // open: value, dp
  Button button_3 ();  // open: out
  Hex_Digit_Display hex_digit_display_3 (.value(clockcircuit_1_seconddigit));  // open: dp
  Hex_Digit_Display hex_digit_display_4 (.value(clockcircuit_1_firstdigit));  // open: dp
  toNineRippleCounter tonineripplecounter_1 ();  // open: CLKIn, NUMOut
  Hex_Digit_Display hex_digit_display_5 ();  // open: value, dp
  Hex_Digit_Display hex_digit_display_6 ();  // open: value, dp
  LED led_1 (.in(clockcircuit_1_clockstatus));
  clockCircuit clockcircuit_1 (
    .CONTROL(button_1_out), .CLOCKStatus(clockcircuit_1_clockstatus),
    .SECONDDigit(clockcircuit_1_seconddigit), .FIRSTDigit(clockcircuit_1_firstdigit));
  Hex_Digit_Display hex_digit_display_7 ();  // open: value, dp
  Hex_Digit_Display hex_digit_display_8 ();  // open: value, dp

  // Notes on the sheet:
  //   Start / Stop
  //   Split
  //   Elapsed Time
  //   Minutes
  //   :
  //   Reset
  //   Seconds
  //   Stopwatch Interface
  //   Minutes
  //   Split Time
  //   :
  //   Clock Started
  //   Seconds
endmodule

module ioClock (
  input  CTRLSTATUSIn,
  input  CLOCKIn,
  output CLOCKSTATUSOut,
  output CLOCKPulse
);

  wire not_1_out, t_ff_1_qn;

  T_Flip_Flop t_ff_1 (.T(CTRLSTATUSIn), .clk(CTRLSTATUSIn), .Q(CLOCKSTATUSOut), .Qn(t_ff_1_qn));  // open: reset, preset
  not not_1 (not_1_out, t_ff_1_qn);
  enablePulse enablepulse_1 (.CLOCKSTATUSIn(not_1_out), .PULSEIn(CLOCKIn), .RESETIn(t_ff_1_qn), .PULSEOut(CLOCKPulse));
endmodule

module enablePulse (
  input  CLOCKSTATUSIn,
  input  PULSEIn,
  input  RESETIn,
  output PULSEOut
);

  wire d_ff_1_q;

  D_Flip_Flop d_ff_1 (.D(CLOCKSTATUSIn), .clk(PULSEIn), .Q(d_ff_1_q), .reset(RESETIn));  // open: Qn, preset
  and and_1 (PULSEOut, PULSEIn, d_ff_1_q);
endmodule

module digitCtrl (
  input  CLOCKIn,
  output [3:0] SECONDDigit,
  output [3:0] FIRSTDigit
);

  toNineRippleCounter tonineripplecounter_1 (.CLKIn(CLOCKIn), .NUMOut(FIRSTDigit));

  assign SECONDDigit = 4'b0000;
endmodule

module toNineRippleCounter (
  input  CLKIn,
  output [3:0] NUMOut
);

  wire and_1_out, and_2_out, and_3_out, j_k_ff_1_q, j_k_ff_2_q, j_k_ff_3_q, j_k_ff_4_q;

  J_K_Flip_Flop j_k_ff_1 (.J(1'b1), .K(1'b1), .clk(CLKIn), .Q(j_k_ff_1_q), .reset(and_3_out));  // open: Qn, preset
  D_Flip_Flop d_ff_1 (.D(j_k_ff_1_q), .clk(CLKIn), .Q(NUMOut[0]));  // open: Qn, preset, reset
  and and_1 (and_1_out, j_k_ff_1_q, j_k_ff_2_q);
  J_K_Flip_Flop j_k_ff_2 (
    .J(j_k_ff_1_q), .K(j_k_ff_1_q), .clk(CLKIn), .Q(j_k_ff_2_q), .reset(and_3_out));  // open: Qn, preset
  D_Flip_Flop d_ff_2 (.D(j_k_ff_2_q), .clk(CLKIn), .Q(NUMOut[1]));  // open: Qn, preset, reset
  and and_2 (and_2_out, and_1_out, j_k_ff_3_q);
  J_K_Flip_Flop j_k_ff_3 (
    .J(and_1_out), .K(and_1_out), .clk(CLKIn), .Q(j_k_ff_3_q), .reset(and_3_out));  // open: Qn, preset
  J_K_Flip_Flop j_k_ff_4 (
    .J(and_2_out), .K(and_2_out), .clk(CLKIn), .Q(j_k_ff_4_q), .reset(and_3_out));  // open: Qn, preset
  D_Flip_Flop d_ff_3 (.D(j_k_ff_3_q), .clk(CLKIn), .Q(NUMOut[2]));  // open: Qn, preset, reset
  and and_3 (and_3_out, j_k_ff_2_q, j_k_ff_4_q);
  D_Flip_Flop d_ff_4 (.D(j_k_ff_4_q), .clk(CLKIn), .Q(NUMOut[3]));  // open: Qn, preset, reset
endmodule

module clockCircuit (
  input  CONTROL,
  output CLOCKStatus,
  output [3:0] SECONDDigit,
  output [3:0] FIRSTDigit
);

  wire CLK_out, ioclock_1_clockpulse;

  Clock CLK (.out(CLK_out));
  ioClock ioclock_1 (
    .CTRLSTATUSIn(CONTROL), .CLOCKIn(CLK_out), .CLOCKSTATUSOut(CLOCKStatus), .CLOCKPulse(ioclock_1_clockpulse));
  digitCtrl digitctrl_1 (.CLOCKIn(ioclock_1_clockpulse), .SECONDDigit(SECONDDigit), .FIRSTDigit(FIRSTDigit));
endmodule
