// Logisim project stage5.circ as structural Verilog: 11 circuits, main circuit main
module main (
);

  wire button_1_out, button_2_out, button_3_out, clockcircuit_1_clockstatus;
  wire [3:0] clockcircuit_1_elapsedtime, clockcircuit_1_elapsedtime_2, clockcircuit_1_elapsedtime_3,
       clockcircuit_1_splittime, clockcircuit_1_splittime_2, clockcircuit_1_splittime_3,
       clockcircuit_1_splittime_4;
  wire [15:12] clockcircuit_1_elapsedtime_4;

  Button button_1 (.out(button_1_out));
  Hex_Digit_Display hex_digit_display_1 (.value(clockcircuit_1_elapsedtime_4));  // open: dp
  Button button_2 (.out(button_2_out));
  Hex_Digit_Display hex_digit_display_2 (.value(clockcircuit_1_elapsedtime_3));  // open: dp
  Button button_3 (.out(button_3_out));
  Hex_Digit_Display hex_digit_display_3 (.value(clockcircuit_1_elapsedtime_2));  // open: dp
  Hex_Digit_Display hex_digit_display_4 (.value(clockcircuit_1_elapsedtime));  // open: dp
  Hex_Digit_Display hex_digit_display_5 (.value(clockcircuit_1_splittime_4));  // open: dp
  Hex_Digit_Display hex_digit_display_6 (.value(clockcircuit_1_splittime_3));  // open: dp
  LED led_1 (.in(clockcircuit_1_clockstatus));
  clockCircuit clockcircuit_1 (
    .RESET(button_3_out), .SPLITIn(button_2_out), .CONTROL(button_1_out),
    .CLOCKStatus(clockcircuit_1_clockstatus),
    .ELAPSEDTime({clockcircuit_1_elapsedtime_4, clockcircuit_1_elapsedtime_3, clockcircuit_1_elapsedtime_2, clockcircuit_1_elapsedtime}),
    .SPLITTime({clockcircuit_1_splittime_4, clockcircuit_1_splittime_3, clockcircuit_1_splittime_2, clockcircuit_1_splittime}));
  Hex_Digit_Display hex_digit_display_7 (.value(clockcircuit_1_splittime_2));  // open: dp
  Hex_Digit_Display hex_digit_display_8 (.value(clockcircuit_1_splittime));  // open: dp

  // Notes on the sheet:
  //   Start / Stop
  //   Split
  //   Elapsed Time
  //   Minutes
  //   :
  //   Reset
  //   Seconds
  //   Stopwatch Interface
  //   Minutes
  //   Split Time
  //   :
  //   Clock Started
  //   Seconds
endmodule

module clockCircuit (
  input  RESET,
  input  SPLITIn,
  input  CONTROL,
  output CLOCKStatus,
  output [15:0] ELAPSEDTime,
  output [15:0] SPLITTime
);

  wire CLK_out, ioclock_1_clockpulseout, ioclock_1_resetout, ioclock_1_splitout;

  Clock CLK (.out(CLK_out));
  ioClock ioclock_1 (
    .RESETIn(RESET), .SPLITIn(SPLITIn), .STARTSTOPIn(CONTROL), .CLOCKIn(CLK_out),
    .CLOCKSTATUSOut(CLOCKStatus), .RESETOut(ioclock_1_resetout), .CLOCKPULSEOut(ioclock_1_clockpulseout),
    .SPLITOut(ioclock_1_splitout));
  digitCtrl digitctrl_1 (
    .RESETIn(ioclock_1_resetout), .CLOCKIn(ioclock_1_clockpulseout), .FIRSTDigit(ELAPSEDTime[3:0]),
    .SECONDDigit(ELAPSEDTime[7:4]), .THIRDDigit(ELAPSEDTime[11:8]), .FORTHDigit(ELAPSEDTime[15:12]));
  splitCtrl splitctrl_1 (
    .FIRSTSPLITNUMIn(ELAPSEDTime[3:0]), .SECONDSPLITNUMIn(ELAPSEDTime[7:4]),
    .THIRDSPLITNUMIn(ELAPSEDTime[11:8]), .FORTHSPLITNUMIn(ELAPSEDTime[15:12]), .RESETIn(RESET),
    .PULSEIn(ioclock_1_splitout), .FIRSTSPLITNUMOut(SPLITTime[3:0]), .SECONDSPLITNUMOut(SPLITTime[7:4]),
    .THIRDSPLITNUMOut(SPLITTime[11:8]), .FORTHSPLITNUMOut(SPLITTime[15:12]));
endmodule

module ioClock (
  input  RESETIn,
  input  SPLITIn,
  input  STARTSTOPIn,
  input  CLOCKIn,
  output CLOCKSTATUSOut,
  output RESETOut,
  output CLOCKPULSEOut,
  output SPLITOut
);

  wire not_1_out, t_ff_1_qn;

  T_Flip_Flop t_ff_1 (
    .T(STARTSTOPIn), .clk(STARTSTOPIn), .Q(CLOCKSTATUSOut), .Qn(t_ff_1_qn), .reset(RESETIn));  // open: preset
  not not_1 (not_1_out, t_ff_1_qn);
  enablePulse enablepulse_1 (.CLOCKSTATUSIn(not_1_out), .PULSEIn(SPLITIn), .RESETIn(t_ff_1_qn), .PULSEOut(SPLITOut));
  enablePulse enablepulse_2 (
    .CLOCKSTATUSIn(not_1_out), .PULSEIn(CLOCKIn), .RESETIn(t_ff_1_qn), .PULSEOut(CLOCKPULSEOut));

  assign RESETOut = RESETIn;
endmodule

module digitCtrl (
  input  RESETIn,
  input  CLOCKIn,
  output [3:0] FIRSTDigit,
  output [3:0] SECONDDigit,
  output [3:0] THIRDDigit,
  output [3:0] FORTHDigit
);

  wire fourbitripplecounter_1_clockout, fourbitripplecounter_1_resetout, fourbitripplecounter_2_resetout,
       fourbitripplecounter_3_resetout, tonextdigit_1_clkout, tonextdigit_1_numsamebool,
       tonextdigit_1_resetout, tonextdigit_2_clkout, tonextdigit_2_resetout, tonextminute_1_clkout,
       tonextminute_1_resetout;

  fourBitRippleCounter fourbitripplecounter_1 (
    .RESETIn(RESETIn), .CLOCKIn(CLOCKIn), .CHANGENUMONIn(4'b1010),
    .RESETOut(fourbitripplecounter_1_resetout), .CLOCKOut(fourbitripplecounter_1_clockout),
    .NUMOut(FIRSTDigit));
  toNextDigit tonextdigit_1 (
    .RESETIn(fourbitripplecounter_1_resetout), .CLKIn(fourbitripplecounter_1_clockout), .NUMIn(FIRSTDigit),
    .CHANGENUMOn(4'b1000), .RESETOut(tonextdigit_1_resetout), .CLKOut(tonextdigit_1_clkout),
    .NUMSAMEBool(tonextdigit_1_numsamebool));
  fourBitRippleCounter fourbitripplecounter_2 (
    .RESETIn(tonextdigit_1_resetout), .CLOCKIn(tonextdigit_1_clkout), .CHANGENUMONIn(4'b0110),
    .RESETOut(fourbitripplecounter_2_resetout), .NUMOut(SECONDDigit));  // open: CLOCKOut
  toNextMinute tonextminute_1 (
    .RESETIn(fourbitripplecounter_2_resetout), .CLKIn(fourbitripplecounter_1_clockout), .NUMIn(SECONDDigit),
    .CHANGENUMOn(4'b0101), .NUMSAMEBOOLIn(tonextdigit_1_numsamebool), .RESETOut(tonextminute_1_resetout),
    .CLKOut(tonextminute_1_clkout));
  fourBitRippleCounter fourbitripplecounter_3 (
    .RESETIn(tonextminute_1_resetout), .CLOCKIn(tonextminute_1_clkout), .CHANGENUMONIn(4'b1010),
    .RESETOut(fourbitripplecounter_3_resetout), .NUMOut(THIRDDigit));  // open: CLOCKOut
  toNextDigit tonextdigit_2 (
    .RESETIn(fourbitripplecounter_3_resetout), .CLKIn(tonextminute_1_clkout), .NUMIn(THIRDDigit),
    .CHANGENUMOn(4'b1000), .RESETOut(tonextdigit_2_resetout), .CLKOut(tonextdigit_2_clkout));  // open: NUMSAMEBool
  fourBitRippleCounter fourbitripplecounter_4 (
    .RESETIn(tonextdigit_2_resetout), .CLOCKIn(tonextdigit_2_clkout), .CHANGENUMONIn(4'b1010),
    .NUMOut(FORTHDigit));  // open: RESETOut, CLOCKOut
endmodule

module splitCtrl (
  input  [3:0] FIRSTSPLITNUMIn,
  input  [3:0] SECONDSPLITNUMIn,
  input  [3:0] THIRDSPLITNUMIn,
  input  [3:0] FORTHSPLITNUMIn,
  input  RESETIn,
  input  PULSEIn,
  output [3:0] FIRSTSPLITNUMOut,
  output [3:0] SECONDSPLITNUMOut,
  output [3:0] THIRDSPLITNUMOut,
  output [3:0] FORTHSPLITNUMOut
);

  displayDigit displaydigit_1 (
    .NUMIn(FIRSTSPLITNUMIn), .PULSEIn(PULSEIn), .RESETIn(RESETIn), .NUMOut(FIRSTSPLITNUMOut));
  displayDigit displaydigit_2 (
    .NUMIn(SECONDSPLITNUMIn), .PULSEIn(PULSEIn), .RESETIn(RESETIn), .NUMOut(SECONDSPLITNUMOut));
  displayDigit displaydigit_3 (
    .NUMIn(THIRDSPLITNUMIn), .PULSEIn(PULSEIn), .RESETIn(RESETIn), .NUMOut(THIRDSPLITNUMOut));
  displayDigit displaydigit_4 (
    .NUMIn(FORTHSPLITNUMIn), .PULSEIn(PULSEIn), .RESETIn(RESETIn), .NUMOut(FORTHSPLITNUMOut));
endmodule

module enablePulse (
  input  CLOCKSTATUSIn,
  input  PULSEIn,
  input  RESETIn,
  output PULSEOut
);

  wire d_ff_1_q;

  D_Flip_Flop d_ff_1 (.D(CLOCKSTATUSIn), .clk(PULSEIn), .Q(d_ff_1_q), .reset(RESETIn));  // open: Qn, preset
  and and_1 (PULSEOut, PULSEIn, d_ff_1_q);
endmodule

module displayDigit (
  input  [3:0] NUMIn,
  input  PULSEIn,
  input  RESETIn,
  output [3:0] NUMOut
);

  D_Flip_Flop d_ff_1 (.D(NUMIn[0]), .clk(PULSEIn), .Q(NUMOut[0]), .reset(RESETIn));  // open: Qn, preset
  D_Flip_Flop d_ff_2 (.D(NUMIn[1]), .clk(PULSEIn), .Q(NUMOut[1]), .reset(RESETIn));  // open: Qn, preset
  D_Flip_Flop d_ff_3 (.D(NUMIn[2]), .clk(PULSEIn), .Q(NUMOut[2]), .reset(RESETIn));  // open: Qn, preset
  D_Flip_Flop d_ff_4 (.D(NUMIn[3]), .clk(PULSEIn), .Q(NUMOut[3]), .reset(RESETIn));  // open: Qn, preset
endmodule

module fourBitComparer (
  input  [3:0] NUM1In,
  input  [3:0] NUM2In,
  output out_3
);

  wire xnor_1_out, xnor_2_out, xnor_3_out, xnor_4_out;

  xnor xnor_1 (xnor_1_out, NUM1In[0], NUM2In[0]);
  xnor xnor_2 (xnor_2_out, NUM1In[1], NUM2In[1]);
  xnor xnor_3 (xnor_3_out, NUM1In[2], NUM2In[2]);
  xnor xnor_4 (xnor_4_out, NUM1In[3], NUM2In[3]);
  and and_1 (out_3, xnor_1_out, xnor_2_out, xnor_3_out, xnor_4_out);
endmodule

module fourBitRippleCounter (
  input  RESETIn,
  input  CLOCKIn,
  input  [3:0] CHANGENUMONIn,
  output RESETOut,
  output CLOCKOut,
  output [3:0] NUMOut
);

  wire and_1_out, and_2_out, fourbitcomparer_1_out_3, or_1_out;
  wire [3:0] j_k_ff_1_q;

  J_K_Flip_Flop j_k_ff_1 (.J(1'b1), .K(1'b1), .clk(CLOCKIn), .Q(j_k_ff_1_q[0]), .reset(or_1_out));  // open: Qn, preset
  and and_1 (and_1_out, j_k_ff_1_q[0], j_k_ff_1_q[1]);
  J_K_Flip_Flop j_k_ff_2 (
    .J(j_k_ff_1_q[0]), .K(j_k_ff_1_q[0]), .clk(CLOCKIn), .Q(j_k_ff_1_q[1]), .reset(or_1_out));  // open: Qn, preset
  and and_2 (and_2_out, and_1_out, j_k_ff_1_q[2]);
  J_K_Flip_Flop j_k_ff_3 (
    .J(and_1_out), .K(and_1_out), .clk(CLOCKIn), .Q(j_k_ff_1_q[2]), .reset(or_1_out));  // open: Qn, preset
  J_K_Flip_Flop j_k_ff_4 (
    .J(and_2_out), .K(and_2_out), .clk(CLOCKIn), .Q(j_k_ff_1_q[3]), .reset(or_1_out));  // open: Qn, preset
  fourBitComparer fourbitcomparer_1 (.NUM1In(CHANGENUMONIn), .NUM2In(j_k_ff_1_q), .out_3(fourbitcomparer_1_out_3));
  or or_1 (or_1_out, fourbitcomparer_1_out_3, RESETIn);
  displayDigit displaydigit_1 (.NUMIn(j_k_ff_1_q), .PULSEIn(CLOCKIn), .RESETIn(RESETIn), .NUMOut(NUMOut));

  assign CLOCKOut = CLOCKIn;
  assign RESETOut = RESETIn;
endmodule

module toNextDigit (
  input  RESETIn,
  input  CLKIn,
  input  [3:0] NUMIn,
  input  [3:0] CHANGENUMOn,
  output RESETOut,
  output CLKOut,
  output NUMSAMEBool
);

  fourBitComparer fourbitcomparer_1 (.NUM1In(NUMIn), .NUM2In(CHANGENUMOn), .out_3(NUMSAMEBool));
  J_K_Flip_Flop j_k_ff_1 (.J(1'b1), .K(NUMSAMEBool), .clk(CLKIn), .Q(CLKOut), .reset(RESETIn));  // open: Qn, preset

  assign RESETOut = RESETIn;
endmodule

module toNextMinute (
  input  RESETIn,
  input  CLKIn,
  input  [3:0] NUMIn,
  input  [3:0] CHANGENUMOn,
  input  NUMSAMEBOOLIn,
  output RESETOut,
  output CLKOut
);

  wire and_1_out, fourbitcomparer_1_out_3;

  fourBitComparer fourbitcomparer_1 (.NUM1In(NUMIn), .NUM2In(CHANGENUMOn), .out_3(fourbitcomparer_1_out_3));
  and and_1 (and_1_out, fourbitcomparer_1_out_3, NUMSAMEBOOLIn);
  J_K_Flip_Flop j_k_ff_1 (.J(1'b1), .K(and_1_out), .clk(CLKIn), .Q(CLKOut), .reset(RESETIn));  // open: Qn, preset

  assign RESETOut = RESETIn;
endmodule
