// Logisim project stage6.circ as structural Verilog: 15 circuits, main circuit main
module main (
);

  wire button_1_out, button_2_out, button_3_out, clockcircuit_1_clockstatus;
  wire [3:0] clockcircuit_1_elapsedtime, clockcircuit_1_elapsedtime_2, clockcircuit_1_elapsedtime_3,
       clockcircuit_1_splittime, clockcircuit_1_splittime_2, clockcircuit_1_splittime_3,
       clockcircuit_1_splittime_4;
  wire [15:0] clockcircuit_1_fifthsplit, clockcircuit_1_firstsplit, clockcircuit_1_forthsplit,
       clockcircuit_1_secondsplit, clockcircuit_1_thirdsplit;
  wire [15:12] clockcircuit_1_elapsedtime_4;

  Button button_1 (.out(button_1_out));
  Hex_Digit_Display hex_digit_display_1 (.value(clockcircuit_1_elapsedtime_4));  // open: dp
  Button button_2 (.out(button_2_out));
  Hex_Digit_Display hex_digit_display_2 (.value(clockcircuit_1_elapsedtime_3));  // open: dp
  Button button_3 (.out(button_3_out));
  Hex_Digit_Display hex_digit_display_3 (.value(clockcircuit_1_elapsedtime_2));  // open: dp
  Hex_Digit_Display hex_digit_display_4 (.value(clockcircuit_1_elapsedtime));  // open: dp
  Hex_Digit_Display hex_digit_display_5 (.value(clockcircuit_1_splittime_4));  // open: dp
  Hex_Digit_Display hex_digit_display_6 (.value(clockcircuit_1_splittime_3));  // open: dp
  LED led_1 (.in(clockcircuit_1_clockstatus));
  clockCircuit clockcircuit_1 (
    .RESET(button_3_out), .SPLITIn(button_2_out), .CONTROL(button_1_out),
    .CLOCKStatus(clockcircuit_1_clockstatus),
    .ELAPSEDTime({clockcircuit_1_elapsedtime_4, clockcircuit_1_elapsedtime_3, clockcircuit_1_elapsedtime_2, clockcircuit_1_elapsedtime}),
    .SPLITTime({clockcircuit_1_splittime_4, clockcircuit_1_splittime_3, clockcircuit_1_splittime_2, clockcircuit_1_splittime}),
    .FIRSTSplit(clockcircuit_1_firstsplit), .SECONDSplit(clockcircuit_1_secondsplit),
    .THIRDSplit(clockcircuit_1_thirdsplit), .FORTHSplit(clockcircuit_1_forthsplit),
    .FIFTHSplit(clockcircuit_1_fifthsplit));
  splitTimeInterface splittimeinterface_1 (
    .FIRSTSPLIT(clockcircuit_1_firstsplit), .SECONDSPLIT(clockcircuit_1_secondsplit),
    .THIRDSPLIT(clockcircuit_1_thirdsplit), .FORTHSPLIT(clockcircuit_1_forthsplit),
    .FIFTHSPLIT(clockcircuit_1_fifthsplit));
  Hex_Digit_Display hex_digit_display_7 (.value(clockcircuit_1_splittime_2));  // open: dp
  Hex_Digit_Display hex_digit_display_8 (.value(clockcircuit_1_splittime));  // open: dp

  // Notes on the sheet:
  //   Start / Stop
  //   Split
  //   Elapsed Time
  //   Minutes
  //   :
  //   Reset
  //   Seconds
  //   Stopwatch Interface
  //   Minutes
  //   Split Time
  //   :
  //   Clock Started
  //   Seconds
endmodule

module clockCircuit (
  input  RESET,
  input  SPLITIn,
  input  CONTROL,
  output CLOCKStatus,
  output [15:0] ELAPSEDTime,
  output [15:0] SPLITTime,
  output [15:0] FIRSTSplit,
  output [15:0] SECONDSplit,
  output [15:0] THIRDSplit,
  output [15:0] FORTHSplit,
  output [15:0] FIFTHSplit
);

  wire CLK_out, ioclock_1_clockpulseout, ioclock_1_resetout, ioclock_1_splitout;

  Clock CLK (.out(CLK_out));
  ioClock ioclock_1 (
    .RESETIn(RESET), .SPLITIn(SPLITIn), .STARTSTOPIn(CONTROL), .CLOCKIn(CLK_out),
    .CLOCKSTATUSOut(CLOCKStatus), .RESETOut(ioclock_1_resetout), .CLOCKPULSEOut(ioclock_1_clockpulseout),
    .SPLITOut(ioclock_1_splitout));
  digitCtrl digitctrl_1 (
    .RESETIn(ioclock_1_resetout), .CLOCKIn(ioclock_1_clockpulseout), .FIRSTDigit(ELAPSEDTime[3:0]),
    .SECONDDigit(ELAPSEDTime[7:4]), .THIRDDigit(ELAPSEDTime[11:8]), .FORTHDigit(ELAPSEDTime[15:12]));
  splitCtrl splitctrl_1 (
    .FIRSTSPLITNUMIn(ELAPSEDTime[3:0]), .SECONDSPLITNUMIn(ELAPSEDTime[7:4]),
    .THIRDSPLITNUMIn(ELAPSEDTime[11:8]), .FORTHSPLITNUMIn(ELAPSEDTime[15:12]), .RESETIn(RESET),
    .PULSEIn(ioclock_1_splitout), .FIRSTSPLITNUMOut(SPLITTime[3:0]), .SECONDSPLITNUMOut(SPLITTime[7:4]),
    .THIRDSPLITNUMOut(SPLITTime[11:8]), .FORTHSPLITNUMOut(SPLITTime[15:12]));
  splitMemoryCircuit splitmemorycircuit_1 (
    .DIGITONEIn(SPLITTime[3:0]), .DIGITTWOIn(SPLITTime[7:4]), .DIGITTHREEIn(SPLITTime[11:8]),
    .DIGITFOURIn(SPLITTime[15:12]), .PULSEIn(ioclock_1_splitout), .RESETIn(RESET), .FIRSTSplit(FIRSTSplit),
    .SECONDSplit(SECONDSplit), .THIRDSplit(THIRDSplit), .FORTHSplit(FORTHSplit), .FIFTHSplit(FIFTHSplit));
endmodule

module splitTimeInterface (
  input  [15:0] FIRSTSPLIT,
  input  [15:0] SECONDSPLIT,
  input  [15:0] THIRDSPLIT,
  input  [15:0] FORTHSPLIT,
  input  [15:0] FIFTHSPLIT
);

  Hex_Digit_Display hex_digit_display_1 (.value(FIRSTSPLIT[15:12]));  // open: dp
  Hex_Digit_Display hex_digit_display_2 (.value(FIRSTSPLIT[11:8]));  // open: dp
  Hex_Digit_Display hex_digit_display_3 (.value(SECONDSPLIT[15:12]));  // open: dp
  Hex_Digit_Display hex_digit_display_4 (.value(SECONDSPLIT[11:8]));  // open: dp
  Hex_Digit_Display hex_digit_display_5 (.value(THIRDSPLIT[15:12]));  // open: dp
  Hex_Digit_Display hex_digit_display_6 (.value(THIRDSPLIT[11:8]));  // open: dp
  Hex_Digit_Display hex_digit_display_7 (.value(FORTHSPLIT[15:12]));  // open: dp
  Hex_Digit_Display hex_digit_display_8 (.value(FORTHSPLIT[11:8]));  // open: dp
  Hex_Digit_Display hex_digit_display_9 (.value(FIFTHSPLIT[15:12]));  // open: dp
  Hex_Digit_Display hex_digit_display_10 (.value(FIFTHSPLIT[11:8]));  // open: dp
  Hex_Digit_Display hex_digit_display_11 (.value(FIRSTSPLIT[7:4]));  // open: dp
  Hex_Digit_Display hex_digit_display_12 (.value(SECONDSPLIT[7:4]));  // open: dp
  Hex_Digit_Display hex_digit_display_13 (.value(THIRDSPLIT[7:4]));  // open: dp
  Hex_Digit_Display hex_digit_display_14 (.value(FORTHSPLIT[7:4]));  // open: dp
  Hex_Digit_Display hex_digit_display_15 (.value(FIFTHSPLIT[7:4]));  // open: dp
  Hex_Digit_Display hex_digit_display_16 (.value(FIRSTSPLIT[3:0]));  // open: dp
  Hex_Digit_Display hex_digit_display_17 (.value(SECONDSPLIT[3:0]));  // open: dp
  Hex_Digit_Display hex_digit_display_18 (.value(THIRDSPLIT[3:0]));  // open: dp
  Hex_Digit_Display hex_digit_display_19 (.value(FORTHSPLIT[3:0]));  // open: dp
  Hex_Digit_Display hex_digit_display_20 (.value(FIFTHSPLIT[3:0]));  // open: dp
endmodule

module ioClock (
  input  RESETIn,
  input  SPLITIn,
  input  STARTSTOPIn,
  input  CLOCKIn,
  output CLOCKSTATUSOut,
  output RESETOut,
  output CLOCKPULSEOut,
  output SPLITOut
);

  wire not_1_out, t_ff_1_qn;

  T_Flip_Flop t_ff_1 (
    .T(STARTSTOPIn), .clk(STARTSTOPIn), .Q(CLOCKSTATUSOut), .Qn(t_ff_1_qn), .reset(RESETIn));  // open: preset
  not not_1 (not_1_out, t_ff_1_qn);
  enablePulse enablepulse_1 (.CLOCKSTATUSIn(not_1_out), .PULSEIn(SPLITIn), .RESETIn(t_ff_1_qn), .PULSEOut(SPLITOut));
  enablePulse enablepulse_2 (
    .CLOCKSTATUSIn(not_1_out), .PULSEIn(CLOCKIn), .RESETIn(t_ff_1_qn), .PULSEOut(CLOCKPULSEOut));

  assign RESETOut = RESETIn;
endmodule

module digitCtrl (
  input  RESETIn,
  input  CLOCKIn,
  output [3:0] FIRSTDigit,
  output [3:0] SECONDDigit,
  output [3:0] THIRDDigit,
  output [3:0] FORTHDigit
);

  wire fourbitripplecounter_1_clockout, fourbitripplecounter_1_resetout, fourbitripplecounter_2_resetout,
       fourbitripplecounter_3_resetout, tonextdigit_1_clkout, tonextdigit_1_numsamebool,
       tonextdigit_1_resetout, tonextdigit_2_clkout, tonextdigit_2_resetout, tonextminute_1_clkout,
       tonextminute_1_resetout;

  fourBitRippleCounter fourbitripplecounter_1 (
    .RESETIn(RESETIn), .CLOCKIn(CLOCKIn), .CHANGENUMONIn(4'b1010),
    .RESETOut(fourbitripplecounter_1_resetout), .CLOCKOut(fourbitripplecounter_1_clockout),
    .NUMOut(FIRSTDigit));
  toNextDigit tonextdigit_1 (
    .RESETIn(fourbitripplecounter_1_resetout), .CLKIn(fourbitripplecounter_1_clockout), .NUMIn(FIRSTDigit),
    .CHANGENUMOn(4'b1000), .RESETOut(tonextdigit_1_resetout), .CLKOut(tonextdigit_1_clkout),
    .NUMSAMEBool(tonextdigit_1_numsamebool));
  fourBitRippleCounter fourbitripplecounter_2 (
    .RESETIn(tonextdigit_1_resetout), .CLOCKIn(tonextdigit_1_clkout), .CHANGENUMONIn(4'b0110),
    .RESETOut(fourbitripplecounter_2_resetout), .NUMOut(SECONDDigit));  // open: CLOCKOut
  toNextMinute tonextminute_1 (
    .RESETIn(fourbitripplecounter_2_resetout), .CLKIn(fourbitripplecounter_1_clockout), .NUMIn(SECONDDigit),
    .CHANGENUMOn(4'b0101), .NUMSAMEBOOLIn(tonextdigit_1_numsamebool), .RESETOut(tonextminute_1_resetout),
    .CLKOut(tonextminute_1_clkout));
  fourBitRippleCounter fourbitripplecounter_3 (
    .RESETIn(tonextminute_1_resetout), .CLOCKIn(tonextminute_1_clkout), .CHANGENUMONIn(4'b1010),
    .RESETOut(fourbitripplecounter_3_resetout), .NUMOut(THIRDDigit));  // open: CLOCKOut
  toNextDigit tonextdigit_2 (
    .RESETIn(fourbitripplecounter_3_resetout), .CLKIn(tonextminute_1_clkout), .NUMIn(THIRDDigit),
    .CHANGENUMOn(4'b1000), .RESETOut(tonextdigit_2_resetout), .CLKOut(tonextdigit_2_clkout));  // open: NUMSAMEBool
  fourBitRippleCounter fourbitripplecounter_4 (
    .RESETIn(tonextdigit_2_resetout), .CLOCKIn(tonextdigit_2_clkout), .CHANGENUMONIn(4'b1010),
    .NUMOut(FORTHDigit));  // open: RESETOut, CLOCKOut
endmodule

module splitCtrl (
  input  [3:0] FIRSTSPLITNUMIn,
  input  [3:0] SECONDSPLITNUMIn,
  input  [3:0] THIRDSPLITNUMIn,
  input  [3:0] FORTHSPLITNUMIn,
  input  RESETIn,
  input  PULSEIn,
  output [3:0] FIRSTSPLITNUMOut,
  output [3:0] SECONDSPLITNUMOut,
  output [3:0] THIRDSPLITNUMOut,
  output [3:0] FORTHSPLITNUMOut
);

  displayDigit displaydigit_1 (
    .NUMIn(FIRSTSPLITNUMIn), .PULSEIn(PULSEIn), .RESETIn(RESETIn), .NUMOut(FIRSTSPLITNUMOut));
  displayDigit displaydigit_2 (
    .NUMIn(SECONDSPLITNUMIn), .PULSEIn(PULSEIn), .RESETIn(RESETIn), .NUMOut(SECONDSPLITNUMOut));
  displayDigit displaydigit_3 (
    .NUMIn(THIRDSPLITNUMIn), .PULSEIn(PULSEIn), .RESETIn(RESETIn), .NUMOut(THIRDSPLITNUMOut));
  displayDigit displaydigit_4 (
    .NUMIn(FORTHSPLITNUMIn), .PULSEIn(PULSEIn), .RESETIn(RESETIn), .NUMOut(FORTHSPLITNUMOut));
endmodule

module fiveBitStack (
  input  BYTEIn,
  input  PULSEIn,
  input  RESETIn,
  output FIFTHBYTEOut,
  output FORTHBYTEOut,
  output THIRDBYTEOut,
  output SECONDBYTEOut,
  output FIRSTBYTEOut
);

  wire and_1_out, and_2_out, and_3_out, and_4_out, and_5_out, and_6_out, and_7_out, and_8_out, and_9_out,
       and_10_out, not_1_out, or_1_out, or_2_out, or_3_out, or_4_out, or_5_out, or_6_out;

  not not_1 (not_1_out, 1'b1);
  and and_1 (and_1_out, 1'b1, 1'b0);
  and and_2 (and_2_out, not_1_out, SECONDBYTEOut);
  or or_1 (or_1_out, and_1_out, and_2_out);
  D_Flip_Flop d_ff_1 (.D(or_1_out), .clk(PULSEIn), .Q(FIRSTBYTEOut), .preset(BYTEIn), .reset(or_2_out));  // open: Qn
  or or_2 (or_2_out, ~BYTEIn, RESETIn);  // OR_Gate
  LED led_1 (.in(FIRSTBYTEOut));
  and and_3 (and_3_out, 1'b1, FIRSTBYTEOut);
  and and_4 (and_4_out, not_1_out, THIRDBYTEOut);
  or or_3 (or_3_out, and_3_out, and_4_out);
  D_Flip_Flop d_ff_2 (.D(or_3_out), .clk(PULSEIn), .Q(SECONDBYTEOut), .reset(RESETIn));  // open: Qn, preset
  LED led_2 (.in(SECONDBYTEOut));
  and and_5 (and_5_out, 1'b1, SECONDBYTEOut);
  and and_6 (and_6_out, not_1_out, FORTHBYTEOut);
  or or_4 (or_4_out, and_5_out, and_6_out);
  D_Flip_Flop d_ff_3 (.D(or_4_out), .clk(PULSEIn), .Q(THIRDBYTEOut), .reset(RESETIn));  // open: Qn, preset
  LED led_3 (.in(THIRDBYTEOut));
  and and_7 (and_7_out, 1'b1, THIRDBYTEOut);
  and and_8 (and_8_out, not_1_out, FIFTHBYTEOut);
  or or_5 (or_5_out, and_7_out, and_8_out);
  D_Flip_Flop d_ff_4 (.D(or_5_out), .clk(PULSEIn), .Q(FORTHBYTEOut), .reset(RESETIn));  // open: Qn, preset
  LED led_4 (.in(FORTHBYTEOut));
  and and_9 (and_9_out, 1'b1, FORTHBYTEOut);
  or or_6 (or_6_out, and_9_out, and_10_out);
  and and_10 (and_10_out, not_1_out, 1'b0);
  D_Flip_Flop d_ff_5 (.D(or_6_out), .clk(PULSEIn), .Q(FIFTHBYTEOut), .reset(RESETIn));  // open: Qn, preset
  LED led_5 (.in(FIFTHBYTEOut));
endmodule

module multiBitStack (
  input  [3:0] DIGITIn,
  input  CLKIn,
  input  RESETIn,
  output [3:0] FIRSTSplit,
  output [3:0] SECONDSplit,
  output [3:0] THIRDSplit,
  output [3:0] FORTHSplit,
  output [3:0] FIFTHSplit
);

  fiveBitStack fivebitstack_1 (
    .BYTEIn(DIGITIn[0]), .PULSEIn(CLKIn), .RESETIn(RESETIn), .FIFTHBYTEOut(FIFTHSplit[0]),
    .FORTHBYTEOut(FORTHSplit[0]), .THIRDBYTEOut(THIRDSplit[0]), .SECONDBYTEOut(SECONDSplit[0]),
    .FIRSTBYTEOut(FIRSTSplit[0]));
  fiveBitStack fivebitstack_2 (
    .BYTEIn(DIGITIn[1]), .PULSEIn(CLKIn), .RESETIn(RESETIn), .FIFTHBYTEOut(FIFTHSplit[1]),
    .FORTHBYTEOut(FORTHSplit[1]), .THIRDBYTEOut(THIRDSplit[1]), .SECONDBYTEOut(SECONDSplit[1]),
    .FIRSTBYTEOut(FIRSTSplit[1]));
  fiveBitStack fivebitstack_3 (
    .BYTEIn(DIGITIn[2]), .PULSEIn(CLKIn), .RESETIn(RESETIn), .FIFTHBYTEOut(FIFTHSplit[2]),
    .FORTHBYTEOut(FORTHSplit[2]), .THIRDBYTEOut(THIRDSplit[2]), .SECONDBYTEOut(SECONDSplit[2]),
    .FIRSTBYTEOut(FIRSTSplit[2]));
  fiveBitStack fivebitstack_4 (
    .BYTEIn(DIGITIn[3]), .PULSEIn(CLKIn), .RESETIn(RESETIn), .FIFTHBYTEOut(FIFTHSplit[3]),
    .FORTHBYTEOut(FORTHSplit[3]), .THIRDBYTEOut(THIRDSplit[3]), .SECONDBYTEOut(SECONDSplit[3]),
    .FIRSTBYTEOut(FIRSTSplit[3]));
endmodule

module splitMemoryCircuit (
  input  [3:0] DIGITONEIn,
  input  [3:0] DIGITTWOIn,
  input  [3:0] DIGITTHREEIn,
  input  [3:0] DIGITFOURIn,
  input  PULSEIn,
  input  RESETIn,
  output [15:0] FIRSTSplit,
  output [15:0] SECONDSplit,
  output [15:0] THIRDSplit,
  output [15:0] FORTHSplit,
  output [15:0] FIFTHSplit
);

  multiBitStack multibitstack_1 (
    .DIGITIn(DIGITONEIn), .CLKIn(PULSEIn), .RESETIn(RESETIn), .FIRSTSplit(FIRSTSplit[3:0]),
    .SECONDSplit(SECONDSplit[3:0]), .THIRDSplit(THIRDSplit[3:0]), .FORTHSplit(FORTHSplit[3:0]),
    .FIFTHSplit(FIFTHSplit[3:0]));
  multiBitStack multibitstack_2 (
    .DIGITIn(DIGITTWOIn), .CLKIn(PULSEIn), .RESETIn(RESETIn), .FIRSTSplit(FIRSTSplit[7:4]),
    .SECONDSplit(SECONDSplit[7:4]), .THIRDSplit(THIRDSplit[7:4]), .FORTHSplit(FORTHSplit[7:4]),
    .FIFTHSplit(FIFTHSplit[7:4]));
  multiBitStack multibitstack_3 (
    .DIGITIn(DIGITTHREEIn), .CLKIn(PULSEIn), .RESETIn(RESETIn), .FIRSTSplit(FIRSTSplit[11:8]),
    .SECONDSplit(SECONDSplit[11:8]), .THIRDSplit(THIRDSplit[11:8]), .FORTHSplit(FORTHSplit[11:8]),
    .FIFTHSplit(FIFTHSplit[11:8]));
  multiBitStack multibitstack_4 (
    .DIGITIn(DIGITFOURIn), .CLKIn(PULSEIn), .RESETIn(RESETIn), .FIRSTSplit(FIRSTSplit[15:12]),
    .SECONDSplit(SECONDSplit[15:12]), .THIRDSplit(THIRDSplit[15:12]), .FORTHSplit(FORTHSplit[15:12]),
    .FIFTHSplit(FIFTHSplit[15:12]));
endmodule

module enablePulse (
  input  CLOCKSTATUSIn,
  input  PULSEIn,
  input  RESETIn,
  output PULSEOut
);

  wire d_ff_1_q;

  D_Flip_Flop d_ff_1 (.D(CLOCKSTATUSIn), .clk(PULSEIn), .Q(d_ff_1_q), .reset(RESETIn));  // open: Qn, preset
  and and_1 (PULSEOut, PULSEIn, d_ff_1_q);
endmodule

module displayDigit (
  input  [3:0] NUMIn,
  input  PULSEIn,
  input  RESETIn,
  output [3:0] NUMOut
);

  D_Flip_Flop d_ff_1 (.D(NUMIn[0]), .clk(PULSEIn), .Q(NUMOut[0]), .reset(RESETIn));  // open: Qn, preset
  D_Flip_Flop d_ff_2 (.D(NUMIn[1]), .clk(PULSEIn), .Q(NUMOut[1]), .reset(RESETIn));  // open: Qn, preset
  D_Flip_Flop d_ff_3 (.D(NUMIn[2]), .clk(PULSEIn), .Q(NUMOut[2]), .reset(RESETIn));  // open: Qn, preset
  D_Flip_Flop d_ff_4 (.D(NUMIn[3]), .clk(PULSEIn), .Q(NUMOut[3]), .reset(RESETIn));  // open: Qn, preset
endmodule

module fourBitComparer (
  input  [3:0] NUM1In,
  input  [3:0] NUM2In,
  output out_3
);

  wire xnor_1_out, xnor_2_out, xnor_3_out, xnor_4_out;

  xnor xnor_1 (xnor_1_out, NUM1In[0], NUM2In[0]);
  xnor xnor_2 (xnor_2_out, NUM1In[1], NUM2In[1]);
  xnor xnor_3 (xnor_3_out, NUM1In[2], NUM2In[2]);
  xnor xnor_4 (xnor_4_out, NUM1In[3], NUM2In[3]);
  and and_1 (out_3, xnor_1_out, xnor_2_out, xnor_3_out, xnor_4_out);
endmodule

module fourBitRippleCounter (
  input  RESETIn,
  input  CLOCKIn,
  input  [3:0] CHANGENUMONIn,
  output RESETOut,
  output CLOCKOut,
  output [3:0] NUMOut
);

  wire and_1_out, and_2_out, fourbitcomparer_1_out_3, or_1_out;
  wire [3:0] j_k_ff_1_q;

  J_K_Flip_Flop j_k_ff_1 (.J(1'b1), .K(1'b1), .clk(CLOCKIn), .Q(j_k_ff_1_q[0]), .reset(or_1_out));  // open: Qn, preset
  and and_1 (and_1_out, j_k_ff_1_q[0], j_k_ff_1_q[1]);
  J_K_Flip_Flop j_k_ff_2 (
    .J(j_k_ff_1_q[0]), .K(j_k_ff_1_q[0]), .clk(CLOCKIn), .Q(j_k_ff_1_q[1]), .reset(or_1_out));  // open: Qn, preset
  and and_2 (and_2_out, and_1_out, j_k_ff_1_q[2]);
  J_K_Flip_Flop j_k_ff_3 (
    .J(and_1_out), .K(and_1_out), .clk(CLOCKIn), .Q(j_k_ff_1_q[2]), .reset(or_1_out));  // open: Qn, preset
  J_K_Flip_Flop j_k_ff_4 (
    .J(and_2_out), .K(and_2_out), .clk(CLOCKIn), .Q(j_k_ff_1_q[3]), .reset(or_1_out));  // open: Qn, preset
  fourBitComparer fourbitcomparer_1 (.NUM1In(CHANGENUMONIn), .NUM2In(j_k_ff_1_q), .out_3(fourbitcomparer_1_out_3));
  or or_1 (or_1_out, fourbitcomparer_1_out_3, RESETIn);
  displayDigit displaydigit_1 (.NUMIn(j_k_ff_1_q), .PULSEIn(CLOCKIn), .RESETIn(RESETIn), .NUMOut(NUMOut));

  assign CLOCKOut = CLOCKIn;
  assign RESETOut = RESETIn;
endmodule

module toNextDigit (
  input  RESETIn,
  input  CLKIn,
  input  [3:0] NUMIn,
  input  [3:0] CHANGENUMOn,
  output RESETOut,
  output CLKOut,
  output NUMSAMEBool
);

  fourBitComparer fourbitcomparer_1 (.NUM1In(NUMIn), .NUM2In(CHANGENUMOn), .out_3(NUMSAMEBool));
  J_K_Flip_Flop j_k_ff_1 (.J(1'b1), .K(NUMSAMEBool), .clk(CLKIn), .Q(CLKOut), .reset(RESETIn));  // open: Qn, preset

  assign RESETOut = RESETIn;
endmodule

module toNextMinute (
  input  RESETIn,
  input  CLKIn,
  input  [3:0] NUMIn,
  input  [3:0] CHANGENUMOn,
  input  NUMSAMEBOOLIn,
  output RESETOut,
  output CLKOut
);

  wire and_1_out, fourbitcomparer_1_out_3;

  fourBitComparer fourbitcomparer_1 (.NUM1In(NUMIn), .NUM2In(CHANGENUMOn), .out_3(fourbitcomparer_1_out_3));
  and and_1 (and_1_out, fourbitcomparer_1_out_3, NUMSAMEBOOLIn);
  J_K_Flip_Flop j_k_ff_1 (.J(1'b1), .K(and_1_out), .clk(CLKIn), .Q(CLKOut), .reset(RESETIn));  // open: Qn, preset

  assign RESETOut = RESETIn;
endmodule
